// Logisim project new_CPU.circ as structural Verilog: 2 circuits, main circuit main
module main (
  input  [3:0] B,
  input  [3:0] A,
  input  [3:0] in_3
);

  ROM #(.dataWidth(12)) rom_1 (.data({in_3, A, B}));  // open: addr
  MyALU myalu_1 ();  // open: Cin, in_2, in_3, in_4, M, out_6, A_B, Sign
  ROM #(.addrWidth(4), .dataWidth(4)) rom_2 ();  // open: addr, data

  // Notes on the sheet:
  //   command
endmodule

module MyALU (
  input  Cin,
  input  [3:0] in_2,
  input  [3:0] in_3,
  input  [3:0] in_4,
  input  M,
  output [3:0] out_6,
  output A_B,
  output Sign
);

  wire n74181_1_p13, n74181_1_p14, n74181_1_p16, n74181_1_p18, not_2_out;

  // _74181 74181_1: pin names not known; wires that end beside it: in_4[0], in_3[1], in_3[0], in_4[1], in_2[3], in_3[2], in_2[2], in_4[2], in_2[1], in_3[3], in_2[0], in_4[3], n74181_1_p13, n74181_1_p14, M, n74181_1_p16, out_6[0], n74181_1_p18, out_6[1], A_B, out_6[2], out_6[3]
  and and_1 (Sign, n74181_1_p14, not_2_out);
  not not_1 (n74181_1_p13, Cin);
  not not_2 (not_2_out, A_B);

  // Notes on the sheet:
  //   Op
  //   A_in
  //   B_in
  //   Output
  //   Cout
  //   Pn
endmodule
